// Logisim project Relatório 4.circ as structural Verilog
module _1__Problema_1 (
  input  in_1,
  input  in_2,
  input  in_3,
  output out_4
);

  wire not_1_out, not_2_out, xor_1_out;

  not not_1 (not_1_out, in_1);
  not not_2 (not_2_out, in_2);
  xor xor_1 (xor_1_out, not_1_out, not_2_out);
  and and_1 (out_4, xor_1_out, in_3);
endmodule

module _2__Problema_2 (
  input  in_1,
  input  in_2,
  input  in_3,
  input  in_4,
  input  in_5,
  input  in_6,
  output out_7,
  output out_8
);

  wire and_1_out, and_2_out, and_3_out, and_4_out, and_5_out, and_6_out, and_7_out, and_8_out, and_9_out,
       and_10_out, not_1_out, not_2_out, not_3_out, not_4_out, not_5_out, not_6_out, not_7_out, or_2_out,
       or_3_out, xnor_1_out, xor_1_out;

  not not_1 (not_1_out, in_1);
  xor xor_1 (xor_1_out, in_2, in_3);
  xnor xnor_1 (xnor_1_out, in_2, in_3);
  not not_2 (not_2_out, in_4);
  not not_3 (not_3_out, in_5);
  not not_4 (not_4_out, in_4);
  not not_5 (not_5_out, in_6);
  not not_6 (not_6_out, in_5);
  not not_7 (not_7_out, in_6);
  and and_1 (and_1_out, not_1_out, xor_1_out);
  and and_2 (and_2_out, in_1, xnor_1_out);
  and and_3 (and_3_out, not_2_out, not_3_out);
  and and_4 (and_4_out, not_4_out, in_5);
  and and_5 (and_5_out, in_4, not_6_out);
  and and_6 (and_6_out, in_4, in_5);
  or or_1 (out_7, and_1_out, and_2_out);
  and and_7 (and_7_out, and_3_out, in_6);
  and and_8 (and_8_out, and_4_out, not_5_out);
  and and_9 (and_9_out, and_5_out, not_7_out);
  and and_10 (and_10_out, and_6_out, in_6);
  or or_2 (or_2_out, and_7_out, and_8_out);
  or or_3 (or_3_out, and_9_out, and_10_out);
  or or_4 (out_8, or_2_out, or_3_out);
endmodule

module _3__Problema_3 (
  input  in_1,
  input  in_2,
  input  in_3,
  input  in_4,
  output out_5
);

  wire and_1_out, and_2_out, or_1_out;

  or or_1 (or_1_out, in_2, in_3);
  and and_1 (and_1_out, in_1, in_2, in_3);
  and and_2 (and_2_out, or_1_out, in_4);
  or or_2 (out_5, and_1_out, and_2_out);
endmodule

module _4__Problema_4 (
  input  in_1,
  input  in_2,
  input  in_3,
  output out_4
);

  wire and_1_out, and_2_out, or_1_out;

  or or_1 (or_1_out, in_1, in_2);
  and and_1 (and_1_out, in_1, in_2);
  and and_2 (and_2_out, or_1_out, in_3);
  or or_2 (out_4, and_1_out, and_2_out);
endmodule

module _5__Problema_5 (
  input  in_1,
  input  in_2,
  input  in_3,
  output out_4
);

  and and_1 (out_4, in_1, in_2);
endmodule

module _6__Problema_6 (
  input  in_1,
  input  in_2,
  input  in_3,
  output out_4
);

  Multiplexer multiplexer_1 (.in0(in_1), .in1(in_2), .out(out_4), .sel(in_3));  // open: en
endmodule
