// Logisim project Relatório 2.circ as structural Verilog
module \_1__Distribuição_com_Inversão__NOT__OR__AND  (
  input  in_1,
  input  in_2,
  input  in_3,
  output out_4
);

  wire and_1_out, not_1_out, not_2_out, or_1_out, or_2_out;

  not not_1 (not_1_out, in_2);
  not not_2 (not_2_out, in_3);
  or or_1 (or_1_out, not_1_out, not_2_out);
  or or_2 (or_2_out, in_2, in_3);
  and and_1 (and_1_out, in_1, or_1_out);
  and and_2 (out_4, and_1_out, or_2_out);
endmodule

module \_2__Combinação_de_Soma_e_Produto__NOT__OR__AND  (
  input  in_1,
  input  in_2,
  input  in_3,
  input  in_4,
  output out_5
);

  wire and_1_out, not_1_out, not_2_out, or_1_out, or_2_out;

  not not_1 (not_1_out, in_3);
  not not_2 (not_2_out, in_2);
  or or_1 (or_1_out, not_2_out, in_4);
  and and_1 (and_1_out, not_1_out, not_1_out, or_1_out);
  or or_2 (or_2_out, in_2, and_1_out);
  and and_2 (out_5, in_1, or_2_out);
endmodule

module \_3__Soma_de_Produtos_com_Inversão__NOT__OR__AND  (
  input  in_1,
  input  in_2,
  input  in_3,
  output out_4
);

  wire and_1_out, and_2_out, not_1_out, not_2_out;

  not not_1 (not_1_out, and_1_out);
  and and_1 (and_1_out, in_1, in_2);
  not not_2 (not_2_out, and_2_out);
  and and_2 (and_2_out, in_2, in_3);
  or or_1 (out_4, not_1_out, not_2_out);
endmodule

module \_4__Anulação_por_Multiplicação__NOT__OR__AND  (
  input  in_1,
  input  in_2,
  output out_3
);

  wire and_1_out, and_2_out, and_3_out, not_1_out, not_2_out, or_1_out, or_2_out;

  not not_1 (not_1_out, in_1);
  and and_1 (and_1_out, in_1, in_2);
  not not_2 (not_2_out, in_2);
  and and_2 (and_2_out, in_2, not_1_out);
  or or_1 (or_1_out, in_1, and_1_out, not_2_out);
  or or_2 (or_2_out, in_1, not_2_out);
  and and_3 (and_3_out, or_2_out, or_1_out);
  and and_4 (out_3, and_2_out, and_3_out);
endmodule

module \_5__Redução_por_Identidade__NOT__OR__AND  (
  input  in_1,
  input  in_2,
  input  in_3,
  input  in_4,
  output out_5
);

  wire and_1_out, and_2_out, and_3_out, and_4_out, and_5_out, not_1_out, not_2_out, not_3_out, or_1_out,
       or_2_out;

  not not_1 (not_1_out, in_1);
  not not_2 (not_2_out, in_3);
  and and_1 (and_1_out, in_3, not_1_out, in_4);
  and and_2 (and_2_out, not_1_out, in_2);
  and and_3 (and_3_out, not_2_out, in_4);
  not not_3 (not_3_out, in_4);
  or or_1 (or_1_out, and_3_out, not_3_out);
  buf or_2 (or_2_out, and_1_out);  // OR_Gate
  and and_4 (and_4_out, or_2_out, in_2);
  and and_5 (and_5_out, and_2_out, or_1_out);
  or or_3 (out_5, and_4_out, and_5_out);
endmodule

module \_6__Absorção_e_Distribuição__NOT__OR__AND  (
  input  in_1,
  input  in_2,
  input  in_3,
  input  in_4,
  output out_5
);

  wire and_1_out, and_2_out, not_1_out, not_2_out, not_3_out, or_1_out, or_2_out;

  not not_1 (not_1_out, in_2);
  or or_1 (or_1_out, not_1_out, in_3);
  not not_2 (not_2_out, or_1_out);
  and and_1 (and_1_out, in_3, in_4);
  and and_2 (and_2_out, in_1, not_2_out);
  not not_3 (not_3_out, and_1_out);
  or or_2 (or_2_out, and_2_out, not_3_out);
  not not_4 (out_5, or_2_out);
endmodule

module \_7__Alarme_Químico  (
  input  in_1,
  input  in_2,
  input  in_3,
  input  in_4,
  output out_5,
  output out_6
);

  wire not_1_out, not_2_out, or_1_out, or_2_out;

  or or_1 (or_1_out, in_2, in_3);
  not not_1 (not_1_out, or_1_out);
  or or_2 (or_2_out, in_3, in_4);
  not not_2 (not_2_out, or_2_out);
  or or_3 (out_5, in_1, not_1_out);
  or or_4 (out_6, in_1, not_2_out);
endmodule

module \_8__Luz_de_Advertência  (
  input  in_1,
  input  in_2,
  input  in_3,
  output out_4
);

  wire not_1_out;

  not not_1 (not_1_out, in_3);
  and and_1 (out_4, in_1, in_2, not_1_out);
endmodule

module _9__Controle_de_Madeira (
  input  in_1,
  input  in_2,
  input  in_3,
  input  in_4,
  output out_5
);

  wire and_1_out, and_2_out, and_3_out, and_4_out, not_1_out, not_2_out, not_3_out, not_4_out, not_5_out,
       not_6_out, not_7_out, not_8_out, not_9_out;

  not not_1 (not_1_out, in_3);
  not not_2 (not_2_out, in_2);
  not not_3 (not_3_out, in_4);
  not not_4 (not_4_out, in_1);
  not not_5 (not_5_out, in_2);
  not not_6 (not_6_out, in_1);
  not not_7 (not_7_out, in_3);
  not not_8 (not_8_out, in_4);
  not not_9 (not_9_out, in_4);
  and and_1 (and_1_out, not_4_out, not_5_out, not_1_out, in_4);
  and and_2 (and_2_out, not_6_out, not_2_out, in_3, not_3_out);
  and and_3 (and_3_out, in_1, not_7_out, not_8_out);
  and and_4 (and_4_out, in_1, in_2, not_9_out);
  or or_1 (out_5, and_1_out, and_2_out, and_3_out, and_4_out);
endmodule

module _10__Porta_do_Elevador (
  input  in_1,
  input  in_2,
  input  in_3,
  input  in_4,
  output out_5
);

  wire and_1_out, and_2_out, and_3_out, not_1_out, not_2_out, not_3_out, not_4_out, not_5_out, not_6_out,
       not_7_out, not_8_out, not_9_out;

  not not_1 (not_1_out, in_2);
  not not_2 (not_2_out, in_2);
  not not_3 (not_3_out, in_1);
  not not_4 (not_4_out, in_1);
  not not_5 (not_5_out, in_4);
  not not_6 (not_6_out, in_1);
  not not_7 (not_7_out, in_3);
  not not_8 (not_8_out, in_4);
  not not_9 (not_9_out, in_3);
  and and_1 (and_1_out, not_4_out, not_5_out, not_1_out, in_3);
  and and_2 (and_2_out, not_6_out, not_2_out, in_4, not_7_out);
  and and_3 (and_3_out, not_3_out, in_2, not_8_out, not_9_out);
  or or_1 (out_5, and_1_out, and_2_out, and_3_out);
endmodule
